# Fritzing sketch UNO-push (saved by Fritzing 0.9.3b)
breadboards: 1

parts:
  S1 = Pushbutton [package="[THT]"]
  R1 = Resistor [tolerance=±5% resistance=1k package=THT]
  Part1 = Arduino Uno (Rev3)

nets (from the schematic view):
  N1: S1.Pin_1, S1.Pin_2, Part1.GND
  N2: S1.Pin_3, S1.Pin_4, R1.Pin_1, Part1.D7
  N3: R1.Pin_0, Part1.5V
