# Fritzing sketch UNO-push-pullup (saved by Fritzing 0.9.3b)
breadboards: 1

parts:
  S1 = Pushbutton [package="[THT]"]
  Part1 = Arduino Uno (Rev3)

nets (from the breadboard view):
  N1: S1.Pin_1, S1.Pin_2, Part1.D7
  N2: S1.Pin_3, S1.Pin_4, Part1.GND
